# Fritzing sketch base_weight (saved by Fritzing 0.9.3b)
breadboards: 1

parts:
  UL = LOAD_CELL [package=1x03]
  UR = LOAD_CELL [package=1x03]
  LR = LOAD_CELL [package=1x03]
  LL = LOAD_CELL [package=1x03]
  Part1 = HX711 Weighing Sensor Module

nets:
  N1: UL.B, LL.B
  N2: UL.W, Part1.E-
  N3: UL.R, UR.R
  N4: UR.B, LR.B
  N5: UR.W, Part1.A-
  N6: LR.W, Part1.E+
  N7: LR.R, LL.R
  N8: LL.W, Part1.A+
